// Logisim project 1607101.circ as structural Verilog: 3 circuits, main circuit 1607101_ALU
module _1607101_ALU (
  input  Cin,
  input  s0,
  input  s1,
  input  A0,
  input  B0,
  input  A1,
  input  B1,
  input  A2,
  input  B2,
  input  A3,
  input  B3,
  input  A4,
  input  B4,
  input  A5,
  input  B5,
  input  A6,
  input  B6,
  input  A7,
  input  B7
);

  wire _1_0_2_yi, _1_0_3_yi, _1_0_4_yi, _1_0_5_yi, _1_0_6_yi, _1_0_7_yi, _1_0_8_yi, _1_0_yi, FA_2_c, FA_2_s,
       FA_3_c, FA_3_s, FA_4_c, FA_4_s, FA_5_c, FA_5_s, FA_6_c, FA_6_s, FA_7_c, FA_7_s, FA_8_c, FA_8_s, FA_c,
       FA_s;

  _1607101_True_complement_1_0 _1_0 (.Bi(B0), .s0(s0), .s1(s1), .Yi(_1_0_yi));
  _1607101_True_complement_1_0 _1_0_2 (.Bi(B1), .s0(s0), .s1(s1), .Yi(_1_0_2_yi));
  _1607101_True_complement_1_0 _1_0_3 (.Bi(B2), .s0(s0), .s1(s1), .Yi(_1_0_3_yi));
  _1607101_True_complement_1_0 _1_0_4 (.Bi(B3), .s0(s0), .s1(s1), .Yi(_1_0_4_yi));
  _1607101_True_complement_1_0 _1_0_5 (.Bi(B4), .s0(s0), .s1(s1), .Yi(_1_0_5_yi));
  _1607101_True_complement_1_0 _1_0_6 (.Bi(B5), .s0(s0), .s1(s1), .Yi(_1_0_6_yi));
  _1607101_True_complement_1_0 _1_0_7 (.Bi(B6), .s0(s0), .s1(s1), .Yi(_1_0_7_yi));
  _1607101_True_complement_1_0 _1_0_8 (.Bi(B7), .s0(s0), .s1(s1), .Yi(_1_0_8_yi));
  _1607101_FA FA (.x(A0), .y(_1_0_yi), .z(Cin), .S(FA_s), .C(FA_c));
  _1607101_FA FA_2 (.x(A1), .y(_1_0_2_yi), .z(FA_c), .S(FA_2_s), .C(FA_2_c));
  _1607101_FA FA_3 (.x(A2), .y(_1_0_3_yi), .z(FA_2_c), .S(FA_3_s), .C(FA_3_c));
  _1607101_FA FA_4 (.x(A3), .y(_1_0_4_yi), .z(FA_3_c), .S(FA_4_s), .C(FA_4_c));
  _1607101_FA FA_5 (.x(A4), .y(_1_0_5_yi), .z(FA_4_c), .S(FA_5_s), .C(FA_5_c));
  _1607101_FA FA_6 (.x(A5), .y(_1_0_6_yi), .z(FA_5_c), .S(FA_6_s), .C(FA_6_c));
  _1607101_FA FA_7 (.x(A6), .y(_1_0_7_yi), .z(FA_6_c), .S(FA_7_s), .C(FA_7_c));
  _1607101_FA FA_8 (.x(A7), .y(_1_0_8_yi), .z(FA_7_c), .S(FA_8_s), .C(FA_8_c));
  LED F0 (.in(FA_s));
  LED F1 (.in(FA_2_s));
  LED F2 (.in(FA_3_s));
  LED F3 (.in(FA_4_s));
  LED F4 (.in(FA_5_s));
  LED F5 (.in(FA_6_s));
  LED F6 (.in(FA_7_s));
  LED F7 (.in(FA_8_s));
  LED Cout (.in(FA_8_c));

  // Notes on the sheet:
  //   C0
  //   1607101
  //   C1
  //   C2
  //   C3
  //   C4
  //   C5
  //   C6
  //   C7
  //   C8
  //   Arithmatic Unit
endmodule

module _1607101_FA (
  input  x,
  input  y,
  input  z,
  output S,
  output C
);

  wire AND_2_out, AND_out, XOR_out;

  xor XOR (XOR_out, x, y);
  and AND (AND_out, x, y);
  xor XOR_2 (S, XOR_out, z);
  and AND_2 (AND_2_out, XOR_out, z);
  or OR (C, AND_2_out, AND_out);

  // Notes on the sheet:
  //   Full Adder
  //   1607101
endmodule

module _1607101_True_complement_1_0 (
  input  Bi,
  input  s0,
  input  s1,
  output Yi
);

  wire AND_2_out, AND_out, not_1_out;

  not not_1 (not_1_out, Bi);
  and AND (AND_out, Bi, s0);
  and AND_2 (AND_2_out, not_1_out, s1);
  or OR (Yi, AND_out, AND_2_out);

  // Notes on the sheet:
  //   NOT
  //   True/complement, one/zero circuit
  //   1607101
endmodule
