// Logisim project 1607101.circ as structural Verilog: 2 circuits, main circuit 1607101_FA
module _1607101_FA (
  input  x,
  input  y,
  input  z,
  output S,
  output C
);

  wire AND_2_out, AND_out, XOR_out;

  xor XOR (XOR_out, x, y);
  and AND (AND_out, x, y);
  xor XOR_2 (S, XOR_out, z);
  and AND_2 (AND_2_out, XOR_out, z);
  or OR (C, AND_2_out, AND_out);

  // Notes on the sheet:
  //   Full Adder
  //   1607101
endmodule

module _1607101_ALU (
  input  Cin,
  input  s2,
  input  s1,
  input  s0,
  input  A0,
  input  B0,
  input  A1,
  input  B1,
  input  A2,
  input  B2,
  input  A3,
  input  B3
);

  wire and_1_out, and_2_out, and_3_out, and_4_out, and_5_out, and_6_out, and_7_out, and_8_out, and_9_out,
       and_10_out, and_11_out, and_12_out, and_13_out, and_14_out, and_15_out, and_16_out, and_17_out,
       and_18_out, and_19_out, and_20_out, and_21_out, and_22_out, and_23_out, n1607101_fa_1_c,
       n1607101_fa_1_s, n1607101_fa_2_c, n1607101_fa_2_s, n1607101_fa_3_c, n1607101_fa_3_s, n1607101_fa_4_c,
       n1607101_fa_4_s, not_1_out, not_2_out, not_3_out, not_4_out, not_5_out, not_6_out, not_7_out,
       or_1_out, or_2_out, or_3_out, or_4_out, or_5_out, or_6_out, or_7_out, or_8_out;

  not not_1 (not_1_out, B0);
  not not_2 (not_2_out, B1);
  not not_3 (not_3_out, B2);
  not not_4 (not_4_out, B3);
  not not_5 (not_5_out, s2);
  not not_6 (not_6_out, s0);
  and and_1 (and_1_out, not_6_out, s1, s2);
  not not_7 (not_7_out, s1);
  and and_2 (and_2_out, not_6_out, not_7_out, s2);
  and and_3 (and_3_out, and_2_out, B0);
  and and_4 (and_4_out, and_1_out, not_1_out);
  and and_5 (and_5_out, B0, s0);
  and and_6 (and_6_out, not_1_out, s1);
  and and_7 (and_7_out, and_2_out, B1);
  and and_8 (and_8_out, and_1_out, not_2_out);
  and and_9 (and_9_out, B1, s0);
  and and_10 (and_10_out, not_2_out, s1);
  and and_11 (and_11_out, and_2_out, B2);
  and and_12 (and_12_out, and_1_out, not_3_out);
  and and_13 (and_13_out, B2, s0);
  and and_14 (and_14_out, not_3_out, s1);
  and and_15 (and_15_out, and_2_out, B3);
  and and_16 (and_16_out, and_1_out, not_4_out);
  and and_17 (and_17_out, B3, s0);
  and and_18 (and_18_out, not_4_out, s1);
  or or_1 (or_1_out, and_3_out, and_4_out, A0);
  or or_2 (or_2_out, and_5_out, and_6_out);
  or or_3 (or_3_out, and_7_out, and_8_out, A1);
  or or_4 (or_4_out, and_9_out, and_10_out);
  or or_5 (or_5_out, and_11_out, and_12_out, A2);
  or or_6 (or_6_out, and_13_out, and_14_out);
  or or_7 (or_7_out, and_15_out, and_16_out, A3);
  or or_8 (or_8_out, and_17_out, and_18_out);
  and and_19 (and_19_out, not_5_out, Cin);
  _1607101_FA u_1607101_fa_1 (.x(or_1_out), .y(or_2_out), .z(and_19_out), .S(n1607101_fa_1_s), .C(n1607101_fa_1_c));
  and and_20 (and_20_out, not_5_out, n1607101_fa_1_c);
  _1607101_FA u_1607101_fa_2 (.x(or_3_out), .y(or_4_out), .z(and_20_out), .S(n1607101_fa_2_s), .C(n1607101_fa_2_c));
  and and_21 (and_21_out, not_5_out, n1607101_fa_2_c);
  _1607101_FA u_1607101_fa_3 (.x(or_5_out), .y(or_6_out), .z(and_21_out), .S(n1607101_fa_3_s), .C(n1607101_fa_3_c));
  and and_22 (and_22_out, not_5_out, n1607101_fa_3_c);
  _1607101_FA u_1607101_fa_4 (.x(or_7_out), .y(or_8_out), .z(and_22_out), .S(n1607101_fa_4_s), .C(n1607101_fa_4_c));
  and and_23 (and_23_out, not_5_out, n1607101_fa_4_c);
  LED F0 (.in(n1607101_fa_1_s));
  LED F1 (.in(n1607101_fa_2_s));
  LED F2 (.in(n1607101_fa_3_s));
  LED F3 (.in(n1607101_fa_4_s));
  LED Cout (.in(and_23_out));

  // Notes on the sheet:
  //   1607101
  //   ALU
endmodule
