// Logisim project 1607101.circ as structural Verilog: 3 circuits, main circuit 1607101_bus_connection
module _1607101_bus_connection (
  input  [3:0] in_1,
  input  Clock,
  input  LOAD,
  input  Clear,
  input  Enable,
  input  Clock_2,
  input  LOAD_2,
  input  Clear_2,
  input  Enable_2,
  input  Clock_3,
  input  LOAD_3,
  input  Clear_3,
  input  Enable_3,
  input  Clock_4,
  input  LOAD_4,
  input  Clear_4,
  input  Enable_4,
  output [3:0] W3_W2_W1_W0
);

  _1607101_buffer_register u_1607101_buffer_register_1 (
    .Clock(Clock), .Clear(Clear), .X3(W3_W2_W1_W0[3]), .X2(W3_W2_W1_W0[2]), .X1(W3_W2_W1_W0[1]),
    .X0(W3_W2_W1_W0[0]), .Y3(W3_W2_W1_W0[3]), .Y2(W3_W2_W1_W0[2]), .Y1(W3_W2_W1_W0[1]), .Y0(W3_W2_W1_W0[0]),
    .LOAD(LOAD_2), .Enable(Enable_2));
  _1607101_buffer_register u_1607101_buffer_register_2 (
    .Clock(Clock_3), .Clear(Clear_3), .X3(W3_W2_W1_W0[3]), .X2(W3_W2_W1_W0[2]), .X1(W3_W2_W1_W0[1]),
    .X0(W3_W2_W1_W0[0]), .Y3(W3_W2_W1_W0[3]), .Y2(W3_W2_W1_W0[2]), .Y1(W3_W2_W1_W0[1]), .Y0(W3_W2_W1_W0[0]),
    .LOAD(LOAD_4), .Enable(Enable_4));
  _1607101_buffer_register u_1607101_buffer_register_3 (
    .Clock(Clock_2), .Clear(Clear_2), .X3(W3_W2_W1_W0[3]), .X2(W3_W2_W1_W0[2]), .X1(W3_W2_W1_W0[1]),
    .X0(W3_W2_W1_W0[0]), .Y3(W3_W2_W1_W0[3]), .Y2(W3_W2_W1_W0[2]), .Y1(W3_W2_W1_W0[1]), .Y0(W3_W2_W1_W0[0]),
    .LOAD(LOAD), .Enable(Enable));
  _1607101_buffer_register u_1607101_buffer_register_4 (
    .Clock(Clock_4), .Clear(Clear_4), .X3(W3_W2_W1_W0[3]), .X2(W3_W2_W1_W0[2]), .X1(W3_W2_W1_W0[1]),
    .X0(W3_W2_W1_W0[0]), .Y3(W3_W2_W1_W0[3]), .Y2(W3_W2_W1_W0[2]), .Y1(W3_W2_W1_W0[1]), .Y0(W3_W2_W1_W0[0]),
    .LOAD(LOAD_3), .Enable(Enable_3));

  // Notes on the sheet:
  //   1607101
  //   A
  //   B
  //   W bus
  //   Fig. 3: Bus connection of buffer register
  //   C
  //   D
endmodule

module _1607101_intermediate (
  input  LOAD,
  input  Xi,
  input  LOAD__prime,
  input  Qi,
  output Di
);

  wire and_1_out, and_2_out;

  and and_1 (and_1_out, LOAD, Xi);
  and and_2 (and_2_out, LOAD__prime, Qi);
  or or_1 (Di, and_1_out, and_2_out);

  // Notes on the sheet:
  //   1607101
endmodule

module _1607101_buffer_register (
  input  X3,
  input  X2,
  input  X1,
  input  X0,
  input  LOAD,
  input  Clock,
  input  Clear,
  input  Enable,
  output Y3,
  output Y2,
  output Y1,
  output Y0
);

  wire d_ff_1_q, d_ff_2_q, d_ff_3_q, d_ff_4_q, n1607101_intermediate_1_di, n1607101_intermediate_2_di,
       n1607101_intermediate_3_di, n1607101_intermediate_4_di, not_1_out;

  D_Flip_Flop d_ff_1 (
    .clk(Clock), .D(n1607101_intermediate_1_di), .Q(d_ff_1_q), .reset(Clear));  // open: Qn, preset, en
  assign Y3 = Enable ? d_ff_1_q : 1'bz;  // Controlled_Buffer controlled_buffer_1
  _1607101_intermediate u_1607101_intermediate_1 (
    .LOAD(LOAD), .Xi(X3), .LOAD__prime(not_1_out), .Qi(d_ff_1_q), .Di(n1607101_intermediate_1_di));
  D_Flip_Flop d_ff_2 (
    .clk(Clock), .D(n1607101_intermediate_2_di), .Q(d_ff_2_q), .reset(Clear));  // open: Qn, preset, en
  assign Y2 = Enable ? d_ff_2_q : 1'bz;  // Controlled_Buffer controlled_buffer_2
  _1607101_intermediate u_1607101_intermediate_2 (
    .LOAD(LOAD), .Xi(X2), .LOAD__prime(not_1_out), .Qi(d_ff_2_q), .Di(n1607101_intermediate_2_di));
  D_Flip_Flop d_ff_3 (
    .clk(Clock), .D(n1607101_intermediate_3_di), .Q(d_ff_3_q), .reset(Clear));  // open: Qn, preset, en
  _1607101_intermediate u_1607101_intermediate_3 (
    .LOAD(LOAD), .Xi(X1), .LOAD__prime(not_1_out), .Qi(d_ff_3_q), .Di(n1607101_intermediate_3_di));
  assign Y1 = Enable ? d_ff_3_q : 1'bz;  // Controlled_Buffer controlled_buffer_3
  D_Flip_Flop d_ff_4 (
    .clk(Clock), .D(n1607101_intermediate_4_di), .Q(d_ff_4_q), .reset(Clear));  // open: Qn, preset, en
  assign Y0 = Enable ? d_ff_4_q : 1'bz;  // Controlled_Buffer controlled_buffer_4
  _1607101_intermediate u_1607101_intermediate_4 (
    .LOAD(LOAD), .Xi(X0), .LOAD__prime(not_1_out), .Qi(d_ff_4_q), .Di(n1607101_intermediate_4_di));
  not not_1 (not_1_out, LOAD);

  // Notes on the sheet:
  //   1607101
  //   Fig. 2: Buffer Register
endmodule
